# Fritzing sketch GC9A01 (saved by Fritzing 0.9.10b)

parts:
  LCD1 = Waveshare 1.28 inch Round 240x240 LCD Display
  Mod1 = Raspberry Pi Pico

nets:
  N1: LCD1.pin_1, Mod1.pin_36
  N2: LCD1.pin2, Mod1.pin_3, Mod1.pin_23
  N3: LCD1.pin3, Mod1.pin_15
  N4: LCD1.pin4, Mod1.pin_14
  N5: LCD1.pin_5, Mod1.pin_12
  N6: LCD1.pin_6, Mod1.pin_11
  N7: LCD1.pin_7, Mod1.pin_16
  N8: LCD1.pin_8, Mod1.pin_29

custom parts:
  Waveshare 1.28 inch Round 240x240 LCD Display: Waveshare 1.28 inch Round 240x240 LCD Display with GC9A01 Controller
  Raspberry Pi Pico: Raspberry Pi Pico. Based around the RP2040 microcontroller the Pico is a low cost microcontroller device bringing Raspberry Pi quality, cost, and easy of use to the microcontroller space. Jan 2021, Split part in to two versions: tht (this one) and SMD. This one will drill holes for a .1 in header in pcb to allow plugging in the module as well as providing pads to solder the module to the top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
