# Fritzing sketch ssd1306 (saved by Fritzing 0.9.10b)
breadboards: 1

parts:
  Mod1 = Raspberry Pi Pico
  パーツ1 = SPI OLED Monochrome 128x64 0.96 inch

nets:
  N1: Mod1.pin_3, Mod1.pin_8, Mod1.pin_13, Mod1.pin_18, Mod1.pin_23, Mod1.pin_28, Mod1.pin_33, Mod1.pin_38, パーツ1.GND
  N2: Mod1.pin_11, パーツ1.DC
  N3: Mod1.pin_12, パーツ1.CS
  N4: Mod1.pin_14, パーツ1.SCK
  N5: Mod1.pin_15, パーツ1.SDA
  N6: Mod1.pin_16, パーツ1.RES
  N7: Mod1.pin_36, パーツ1.VDD

custom parts:
  Raspberry Pi Pico: Raspberry Pi Pico. Based around the RP2040 microcontroller the Pico is a low cost microcontroller device bringing Raspberry Pi quality, cost, and easy of use to the microcontroller space. Jan 2021, Split part in to two versions: tht (this one) and SMD. This one will drill holes for a .1 in header in pcb to allow plugging in the module as well as providing pads to solder the module to the top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
  SPI OLED Monochrome 128x64 0.96 inch: Unknown 128x64 0.96 inch 128x64 SPI Monochrome OLED display
